// Logisim project 0 a 999.OFICIAL.circ as structural Verilog
module _0_a_9 (
  input  Q0,
  input  Q1,
  input  Q2,
  input  Q3,
  output A,
  output B,
  output C,
  output D,
  output E,
  output F,
  output G
);

  wire and_1_out, and_2_out, and_3_out, and_4_out, and_5_out, and_6_out, and_7_out, and_8_out, and_9_out,
       and_10_out, and_11_out, and_12_out, and_13_out, and_14_out, and_15_out, and_16_out, and_17_out,
       not_1_out, not_2_out, not_3_out, not_4_out, not_5_out, not_6_out, not_7_out, not_8_out, not_9_out,
       not_10_out, not_11_out, not_12_out, not_13_out, not_14_out, not_15_out, not_16_out, not_17_out,
       not_18_out, not_19_out, not_20_out, not_21_out, not_22_out;

  not not_1 (not_1_out, Q1);
  and and_1 (and_1_out, not_1_out, not_2_out);
  not not_2 (not_2_out, Q3);
  not not_3 (not_3_out, Q1);
  and and_2 (and_2_out, not_3_out, Q2);
  and and_3 (and_3_out, Q1, Q3);
  not not_4 (not_4_out, Q1);
  not not_5 (not_5_out, Q2);
  and and_4 (and_4_out, not_5_out, not_6_out);
  not not_6 (not_6_out, Q3);
  and and_5 (and_5_out, Q2, Q3);
  not not_7 (not_7_out, Q2);
  or or_1 (C, not_7_out, Q3, Q1);
  not not_8 (not_8_out, Q1);
  and and_6 (and_6_out, not_8_out, not_9_out);
  not not_9 (not_9_out, Q3);
  not not_10 (not_10_out, Q1);
  and and_7 (and_7_out, not_10_out, Q2);
  and and_8 (and_8_out, Q2, not_11_out);
  not not_11 (not_11_out, Q3);
  and and_9 (and_9_out, Q1, not_12_out, Q3);
  not not_12 (not_12_out, Q2);
  not not_13 (not_13_out, Q1);
  and and_10 (and_10_out, not_13_out, not_14_out);
  not not_14 (not_14_out, Q3);
  and and_11 (and_11_out, Q2, not_15_out);
  not not_15 (not_15_out, Q3);
  not not_16 (not_16_out, Q2);
  and and_12 (and_12_out, not_16_out, not_17_out);
  not not_17 (not_17_out, Q3);
  and and_13 (and_13_out, Q1, not_18_out);
  not not_18 (not_18_out, Q2);
  and and_14 (and_14_out, Q1, not_19_out);
  not not_19 (not_19_out, Q3);
  not not_20 (not_20_out, Q1);
  and and_15 (and_15_out, not_20_out, Q2);
  and and_16 (and_16_out, Q1, not_21_out);
  not not_21 (not_21_out, Q2);
  and and_17 (and_17_out, Q1, not_22_out);
  not not_22 (not_22_out, Q3);
  or or_2 (A, and_1_out, and_2_out, and_3_out, Q0);
  or or_3 (B, not_4_out, and_4_out, and_5_out);
  or or_4 (D, and_6_out, and_7_out, and_8_out, and_9_out);
  or or_5 (E, and_10_out, and_11_out);
  or or_6 (F, and_12_out, and_13_out, and_14_out, Q0);
  or or_7 (G, and_15_out, and_16_out, and_17_out, Q0);
endmodule

module _0_a_999 (
  input  CLOCK
);

  wire and_1_out, and_2_out, and_3_out, clock_1_out, j_k_ff_1_q, j_k_ff_1_qn, j_k_ff_2_q, j_k_ff_2_qn,
       j_k_ff_3_q, j_k_ff_3_qn, j_k_ff_4_q, j_k_ff_4_qn, j_k_ff_5_q, j_k_ff_5_qn, j_k_ff_6_q, j_k_ff_6_qn,
       j_k_ff_7_q, j_k_ff_7_qn, j_k_ff_8_q, j_k_ff_8_qn, j_k_ff_9_q, j_k_ff_9_qn, j_k_ff_10_q, j_k_ff_10_qn,
       j_k_ff_11_q, j_k_ff_11_qn, j_k_ff_12_q, n0_a_9_1_a, n0_a_9_1_b, n0_a_9_1_c, n0_a_9_1_d, n0_a_9_1_e,
       n0_a_9_1_f, n0_a_9_1_g, n0_a_9_2_a, n0_a_9_2_b, n0_a_9_2_c, n0_a_9_2_d, n0_a_9_2_e, n0_a_9_2_f,
       n0_a_9_2_g, n0_a_9_3_a, n0_a_9_3_b, n0_a_9_3_c, n0_a_9_3_d, n0_a_9_3_e, n0_a_9_3_f, n0_a_9_3_g;

  Clock clock_1 (.out(clock_1_out));
  J_K_Flip_Flop j_k_ff_1 (
    .J(CLOCK), .clk(clock_1_out), .K(CLOCK), .Q(j_k_ff_1_q), .Qn(j_k_ff_1_qn), .en(CLOCK), .reset(and_1_out));  // open: preset
  J_K_Flip_Flop j_k_ff_2 (
    .J(CLOCK), .clk(j_k_ff_10_qn), .K(CLOCK), .Q(j_k_ff_2_q), .Qn(j_k_ff_2_qn), .en(CLOCK), .reset(and_2_out));  // open: preset
  J_K_Flip_Flop j_k_ff_3 (
    .J(CLOCK), .clk(j_k_ff_1_qn), .K(CLOCK), .Q(j_k_ff_3_q), .Qn(j_k_ff_3_qn), .en(CLOCK), .reset(and_1_out));  // open: preset
  J_K_Flip_Flop j_k_ff_4 (
    .J(CLOCK), .clk(j_k_ff_11_qn), .K(CLOCK), .Q(j_k_ff_4_q), .Qn(j_k_ff_4_qn), .en(CLOCK), .reset(and_3_out));  // open: preset
  J_K_Flip_Flop j_k_ff_5 (
    .J(CLOCK), .clk(j_k_ff_2_qn), .K(CLOCK), .Q(j_k_ff_5_q), .Qn(j_k_ff_5_qn), .en(CLOCK), .reset(and_2_out));  // open: preset
  J_K_Flip_Flop j_k_ff_6 (
    .J(CLOCK), .clk(j_k_ff_3_qn), .K(CLOCK), .Q(j_k_ff_6_q), .Qn(j_k_ff_6_qn), .en(CLOCK), .reset(and_1_out));  // open: preset
  J_K_Flip_Flop j_k_ff_7 (
    .J(CLOCK), .clk(j_k_ff_4_qn), .K(CLOCK), .Q(j_k_ff_7_q), .Qn(j_k_ff_7_qn), .en(CLOCK), .reset(and_3_out));  // open: preset
  J_K_Flip_Flop j_k_ff_8 (
    .J(CLOCK), .clk(j_k_ff_5_qn), .K(CLOCK), .Q(j_k_ff_8_q), .Qn(j_k_ff_8_qn), .en(CLOCK), .reset(and_2_out));  // open: preset
  J_K_Flip_Flop j_k_ff_9 (
    .J(CLOCK), .clk(j_k_ff_7_qn), .K(CLOCK), .Q(j_k_ff_9_q), .Qn(j_k_ff_9_qn), .en(CLOCK), .reset(and_3_out));  // open: preset
  J_K_Flip_Flop j_k_ff_10 (
    .J(CLOCK), .clk(j_k_ff_6_qn), .K(CLOCK), .Q(j_k_ff_10_q), .Qn(j_k_ff_10_qn), .en(CLOCK), .reset(and_1_out));  // open: preset
  J_K_Flip_Flop j_k_ff_11 (
    .J(CLOCK), .clk(j_k_ff_8_qn), .K(CLOCK), .Q(j_k_ff_11_q), .Qn(j_k_ff_11_qn), .en(CLOCK), .reset(and_2_out));  // open: preset
  _0_a_9 u_0_a_9_1 (
    .Q0(j_k_ff_10_q), .Q1(j_k_ff_6_q), .Q2(j_k_ff_3_q), .Q3(j_k_ff_1_q), .A(n0_a_9_1_a), .B(n0_a_9_1_b),
    .C(n0_a_9_1_c), .D(n0_a_9_1_d), .E(n0_a_9_1_e), .F(n0_a_9_1_f), .G(n0_a_9_1_g));
  J_K_Flip_Flop j_k_ff_12 (
    .J(CLOCK), .clk(j_k_ff_9_qn), .K(CLOCK), .Q(j_k_ff_12_q), .en(CLOCK), .reset(and_3_out));  // open: Qn, preset
  _7_Segment_Display u_7_segment_display_1 (
    .g(n0_a_9_1_g), .f(n0_a_9_1_f), .a(n0_a_9_1_a), .b(n0_a_9_1_b), .e(n0_a_9_1_e), .d(n0_a_9_1_d),
    .c(n0_a_9_1_c));  // open: dp
  and and_1 (and_1_out, j_k_ff_10_q, j_k_ff_3_q);
  _0_a_9 u_0_a_9_2 (
    .Q0(j_k_ff_11_q), .Q1(j_k_ff_8_q), .Q2(j_k_ff_5_q), .Q3(j_k_ff_2_q), .A(n0_a_9_2_a), .B(n0_a_9_2_b),
    .C(n0_a_9_2_c), .D(n0_a_9_2_d), .E(n0_a_9_2_e), .F(n0_a_9_2_f), .G(n0_a_9_2_g));
  and and_2 (and_2_out, j_k_ff_11_q, j_k_ff_5_q);
  _7_Segment_Display u_7_segment_display_2 (
    .g(n0_a_9_2_g), .f(n0_a_9_2_f), .a(n0_a_9_2_a), .b(n0_a_9_2_b), .e(n0_a_9_2_e), .d(n0_a_9_2_d),
    .c(n0_a_9_2_c));  // open: dp
  _0_a_9 u_0_a_9_3 (
    .Q0(j_k_ff_12_q), .Q1(j_k_ff_9_q), .Q2(j_k_ff_7_q), .Q3(j_k_ff_4_q), .A(n0_a_9_3_a), .B(n0_a_9_3_b),
    .C(n0_a_9_3_c), .D(n0_a_9_3_d), .E(n0_a_9_3_e), .F(n0_a_9_3_f), .G(n0_a_9_3_g));
  and and_3 (and_3_out, j_k_ff_12_q, j_k_ff_7_q);
  _7_Segment_Display u_7_segment_display_3 (
    .g(n0_a_9_3_g), .f(n0_a_9_3_f), .a(n0_a_9_3_a), .b(n0_a_9_3_b), .e(n0_a_9_3_e), .d(n0_a_9_3_d),
    .c(n0_a_9_3_c));  // open: dp
endmodule
